# Fritzing sketch schema (saved by Fritzing 0.9.3b)
breadboards: 1

parts:
  Composant1 = Arduino Mega 2560 (Rev3)
  LED1 = LED - 5mm [color="Red (633nm)" package="5 mm [THT]"]
  LED2 = LED - 5mm [color="Red (633nm)" package="5 mm [THT]"]
  LED3 = LED - 5mm [color="Red (633nm)" package="5 mm [THT]"]
  R3 = Resistor [tolerance=±5% resistance=220k package=THT]
  R4 = Resistor [tolerance=±5% resistance=220k package=THT]
  R5 = Resistor [tolerance=±5% resistance=220k package=THT]
  S1 = Pushbutton [package="[THT]"]
  R6 = Resistor [tolerance=±5% resistance=10k package=THT]
  J1 = Piezo Speaker
  R7 = Resistor [tolerance=±5% resistance=100 package=THT]

nets:
  N1: Composant1.GND, R3.Pin_1, R4.Pin_1, R5.Pin_1, R6.Pin_1, R7.Pin_1
  N2: Composant1.D13_PWM, S1.Pin_1, S1.Pin_2, R6.Pin_0
  N3: Composant1.5V, S1.Pin_3, S1.Pin_4
  N4: Composant1.D2_PWM, J1.pin2
  N5: Composant1.D5_PWM, LED3.anode
  N6: Composant1.D6_PWM, LED2.anode
  N7: Composant1.D7_PWM, LED1.anode
  N8: LED1.cathode, R5.Pin_0
  N9: LED2.cathode, R4.Pin_0
  N10: LED3.cathode, R3.Pin_0
  N11: J1.pin1, R7.Pin_0
